// Logisim project imm_gen.circ as structural Verilog: 6 circuits, main circuit imm_gen
module imm_gen (
  input  [31:0] inst,
  input  [2:0] ImmSel,
  output [31:0] imm
);

  Itype itype_1 (.inst(inst), .imm(imm));

  // Notes on the sheet:
  //   INPUTS to your circuit
  //   DON'T CHANGE THE LOCATIONS OF THE INPUTS AND OUTPUTS!
  //   OUTPUT from your circuit
endmodule

module Stype (
  input  [31:0] inst,
  output [31:0] imm
);

  assign imm = {{20{inst[31]}}, {inst[31:25], inst[11:7]}};  // Bit_Extender bit_extender_1
endmodule

module Btype (
  input  [31:0] inst,
  output [31:0] imm
);

  assign imm = {{19{inst[31]}}, {inst[31], inst[7], inst[30:25], inst[11:8], 1'b0}};  // Bit_Extender bit_extender_1
endmodule

module Jtype (
  input  [31:0] inst,
  output [31:0] imm
);

  assign imm = {{12{inst[20]}}, {inst[20], inst[10:1], inst[11], inst[19:12]}};  // Bit_Extender bit_extender_1
endmodule

module Itype (
  input  [31:0] inst,
  output [31:0] imm
);

  assign imm = {{20{inst[31]}}, inst[31:20]};  // Bit_Extender bit_extender_1
endmodule

module Utype (
  input  [31:0] inst,
  output [31:0] imm
);

  assign imm = {{12{1'b0}}, inst[31:12]};  // Bit_Extender bit_extender_1
endmodule
